// Logisim project ALU.circ as structural Verilog: 19 circuits, main circuit main
module main (
);

  wire [3:0] undriven_3;
  wire [4:0] alu_8bit_1_d;
  wire [7:0] alu_8bit_1_r, undriven, undriven_2;

  // Probe on undriven
  // DipSwitch A: pin names not known
  // Probe on undriven_2
  // DipSwitch B: pin names not known
  // Probe on undriven_3
  // DipSwitch #(.number(4)) F: pin names not known
  ALU_8Bit alu_8bit_1 (.A(undriven), .B(undriven_2), .F(undriven_3), .R(alu_8bit_1_r), .D(alu_8bit_1_d));
  // Probe on alu_8bit_1_r
  // Probe on alu_8bit_1_d
endmodule

module ALU_8Bit (
  input  [7:0] A,
  input  [7:0] B,
  input  [3:0] F,
  output [7:0] R,
  output [4:0] D
);

  wire [7:0] adder_8bit_1_sum, and_8bit_1_out_and, gate_8bit_1_out_gate, inverter_8bit_1_out_invert,
       or_8bit_1_out_or, xor_8bit_1_out_xor;

  Inverter_8Bit inverter_8bit_1 (.A(A), .Invert(F[3]), .Out_Invert(inverter_8bit_1_out_invert));
  Gate_8Bit gate_8bit_1 (.A(B), .Enable(F[2]), .Out_Gate(gate_8bit_1_out_gate));
  AND_8Bit and_8bit_1 (.A(inverter_8bit_1_out_invert), .B(gate_8bit_1_out_gate), .Out_AND(and_8bit_1_out_and));
  OR_8Bit or_8bit_1 (.A(inverter_8bit_1_out_invert), .B(gate_8bit_1_out_gate), .Out_OR(or_8bit_1_out_or));
  XOR_8Bit xor_8bit_1 (.A(inverter_8bit_1_out_invert), .B(gate_8bit_1_out_gate), .Out_XOR(xor_8bit_1_out_xor));
  Adder_8Bit adder_8bit_1 (
    .A(inverter_8bit_1_out_invert), .CarryIn(F[3]), .B(gate_8bit_1_out_gate), .Sum(adder_8bit_1_sum),
    .Overflow(D[0]), .CarryOut(D[1]));
  Multiplexer #(.select(2), .width(8)) multiplexer_1 (
    .in0(and_8bit_1_out_and), .in1(or_8bit_1_out_or), .in2(xor_8bit_1_out_xor), .in3(adder_8bit_1_sum),
    .out(R), .sel(F[1:0]));
  isZero_8Bit iszero_8bit_1 (.A(R), .isZero(D[2]));
  SignFlag signflag_1 (.A(R), .Out_Sign(D[3]));
  ParityFlag parityflag_1 (.A(R), .Out_Parity(D[4]));
endmodule

module AND_8Bit (
  input  [7:0] A,
  input  [7:0] B,
  output [7:0] Out_AND
);

  and and_1 (Out_AND[0], A[0], B[0]);
  and and_2 (Out_AND[1], A[1], B[1]);
  and and_3 (Out_AND[2], A[2], B[2]);
  and and_4 (Out_AND[3], A[3], B[3]);
  and and_5 (Out_AND[4], A[4], B[4]);
  and and_6 (Out_AND[5], A[5], B[5]);
  and and_7 (Out_AND[6], A[6], B[6]);
  and and_8 (Out_AND[7], A[7], B[7]);
endmodule

module OR_8Bit (
  input  [7:0] A,
  input  [7:0] B,
  output [7:0] Out_OR
);

  or or_1 (Out_OR[0], A[0], B[0]);
  or or_2 (Out_OR[1], A[1], B[1]);
  or or_3 (Out_OR[2], A[2], B[2]);
  or or_4 (Out_OR[3], A[3], B[3]);
  or or_5 (Out_OR[4], A[4], B[4]);
  or or_6 (Out_OR[5], A[5], B[5]);
  or or_7 (Out_OR[6], A[6], B[6]);
  or or_8 (Out_OR[7], A[7], B[7]);
endmodule

module XOR_8Bit (
  input  [7:0] A,
  input  [7:0] B,
  output [7:0] Out_XOR
);

  xor xor_1 (Out_XOR[0], A[0], B[0]);
  xor xor_2 (Out_XOR[1], A[1], B[1]);
  xor xor_3 (Out_XOR[2], A[2], B[2]);
  xor xor_4 (Out_XOR[3], A[3], B[3]);
  xor xor_5 (Out_XOR[4], A[4], B[4]);
  xor xor_6 (Out_XOR[5], A[5], B[5]);
  xor xor_7 (Out_XOR[6], A[6], B[6]);
  xor xor_8 (Out_XOR[7], A[7], B[7]);
endmodule

module Inverter_8Bit (
  input  [7:0] A,
  input  Invert,
  output [7:0] Out_Invert
);

  xor xor_1 (Out_Invert[0], A[0], Invert);
  xor xor_2 (Out_Invert[1], A[1], Invert);
  xor xor_3 (Out_Invert[2], A[2], Invert);
  xor xor_4 (Out_Invert[3], A[3], Invert);
  xor xor_5 (Out_Invert[4], A[4], Invert);
  xor xor_6 (Out_Invert[5], A[5], Invert);
  xor xor_7 (Out_Invert[6], A[6], Invert);
  xor xor_8 (Out_Invert[7], A[7], Invert);
endmodule

module Gate_8Bit (
  input  [7:0] A,
  input  Enable,
  output [7:0] Out_Gate
);

  and and_1 (Out_Gate[0], A[0], Enable);
  and and_2 (Out_Gate[1], A[1], Enable);
  and and_3 (Out_Gate[2], A[2], Enable);
  and and_4 (Out_Gate[3], A[3], Enable);
  and and_5 (Out_Gate[4], A[4], Enable);
  and and_6 (Out_Gate[5], A[5], Enable);
  and and_7 (Out_Gate[6], A[6], Enable);
  and and_8 (Out_Gate[7], A[7], Enable);
endmodule

module Adder_8Bit (
  input  [7:0] A,
  input  CarryIn,
  input  [7:0] B,
  output [7:0] Sum,
  output Overflow,
  output CarryOut
);

  wire adder_1bit_1_carryout, adder_1bit_2_carryout, adder_1bit_3_carryout, adder_1bit_4_carryout,
       adder_1bit_5_carryout, adder_1bit_6_carryout, adder_1bit_7_carryout;

  Adder_1Bit adder_1bit_1 (.A(A[0]), .B(B[0]), .CarryIn(CarryIn), .CarryOut(adder_1bit_1_carryout), .Sum(Sum[0]));
  Adder_1Bit adder_1bit_2 (
    .A(A[1]), .B(B[1]), .CarryIn(adder_1bit_1_carryout), .CarryOut(adder_1bit_2_carryout), .Sum(Sum[1]));
  Adder_1Bit adder_1bit_3 (
    .A(A[2]), .B(B[2]), .CarryIn(adder_1bit_2_carryout), .CarryOut(adder_1bit_3_carryout), .Sum(Sum[2]));
  Adder_1Bit adder_1bit_4 (
    .A(A[3]), .B(B[3]), .CarryIn(adder_1bit_3_carryout), .CarryOut(adder_1bit_4_carryout), .Sum(Sum[3]));
  Adder_1Bit adder_1bit_5 (
    .A(A[4]), .B(B[4]), .CarryIn(adder_1bit_4_carryout), .CarryOut(adder_1bit_5_carryout), .Sum(Sum[4]));
  Adder_1Bit adder_1bit_6 (
    .A(A[5]), .B(B[5]), .CarryIn(adder_1bit_5_carryout), .CarryOut(adder_1bit_6_carryout), .Sum(Sum[5]));
  Adder_1Bit adder_1bit_7 (
    .A(A[6]), .B(B[6]), .CarryIn(adder_1bit_6_carryout), .CarryOut(adder_1bit_7_carryout), .Sum(Sum[6]));
  Adder_1Bit adder_1bit_8 (.A(A[7]), .B(B[7]), .CarryIn(adder_1bit_7_carryout), .CarryOut(CarryOut), .Sum(Sum[7]));
  xor xor_1 (Overflow, adder_1bit_7_carryout, CarryOut);
endmodule

module Adder_1Bit (
  input  A,
  input  B,
  input  CarryIn,
  output CarryOut,
  output Sum
);

  wire and_1_out, and_2_out, xor_1_out;

  and and_1 (and_1_out, A, B);
  xor xor_1 (xor_1_out, A, B);
  and and_2 (and_2_out, xor_1_out, CarryIn);
  xor xor_2 (Sum, xor_1_out, CarryIn);
  or or_1 (CarryOut, and_1_out, and_2_out);
endmodule

module isZero_8Bit (
  input  [7:0] A,
  output isZero
);

  nor nor_1 (isZero, A[0], A[1], A[2], A[3], A[4], A[5], A[6], A[7]);
endmodule

module Test_AND_8Bit (
);

  wire [7:0] and_8bit_1_out_and, undriven, undriven_2;

  // DipSwitch A: pin names not known
  // DipSwitch B: pin names not known
  // Probe on and_8bit_1_out_and
  AND_8Bit and_8bit_1 (.A(undriven), .B(undriven_2), .Out_AND(and_8bit_1_out_and));
endmodule

module Test_OR_8Bit (
);

  wire [7:0] or_8bit_1_out_or, undriven, undriven_2;

  // DipSwitch A: pin names not known
  // DipSwitch B: pin names not known
  // Probe on or_8bit_1_out_or
  OR_8Bit or_8bit_1 (.A(undriven), .B(undriven_2), .Out_OR(or_8bit_1_out_or));
endmodule

module Test_XOR_8Bit (
);

  wire [7:0] undriven, undriven_2, xor_8bit_1_out_xor;

  // DipSwitch A: pin names not known
  // DipSwitch B: pin names not known
  // Probe on xor_8bit_1_out_xor
  XOR_8Bit xor_8bit_1 (.A(undriven), .B(undriven_2), .Out_XOR(xor_8bit_1_out_xor));
endmodule

module Test_Inverter_8Bit (
);

  wire button_1_out;
  wire [7:0] inverter_8bit_1_out_invert, undriven;

  // DipSwitch A: pin names not known
  Button button_1 (.out(button_1_out));
  // Probe on inverter_8bit_1_out_invert
  Inverter_8Bit inverter_8bit_1 (.A(undriven), .Invert(button_1_out), .Out_Invert(inverter_8bit_1_out_invert));
endmodule

module Test_Gate_8Bit (
);

  wire button_1_out;
  wire [7:0] gate_8bit_1_out_gate, undriven;

  // DipSwitch A: pin names not known
  Button button_1 (.out(button_1_out));
  // Probe on gate_8bit_1_out_gate
  Gate_8Bit gate_8bit_1 (.A(undriven), .Enable(button_1_out), .Out_Gate(gate_8bit_1_out_gate));
endmodule

module Test_Adder_8Bit (
);

  wire adder_8bit_1_carryout, adder_8bit_1_overflow;
  wire [7:0] adder_8bit_1_sum, undriven, undriven_2;

  // DipSwitch A: pin names not known
  // DipSwitch B: pin names not known
  // Probe on undriven_2
  // Probe on undriven
  Adder_8Bit adder_8bit_1 (
    .A(undriven_2), .CarryIn(1'b0), .B(undriven), .Sum(adder_8bit_1_sum), .Overflow(adder_8bit_1_overflow),
    .CarryOut(adder_8bit_1_carryout));
  // Probe on adder_8bit_1_sum
  // Probe on adder_8bit_1_overflow
  // Probe on adder_8bit_1_carryout
endmodule

module Test_Add_Sub_8Bit (
);

  wire adder_8bit_1_overflow, button_1_out;
  wire [7:0] adder_8bit_1_sum, inverter_8bit_1_out_invert, undriven, undriven_2;

  // Probe on undriven
  // DipSwitch A: pin names not known
  // DipSwitch B: pin names not known
  Button button_1 (.out(button_1_out));
  Inverter_8Bit inverter_8bit_1 (.A(undriven), .Invert(button_1_out), .Out_Invert(inverter_8bit_1_out_invert));
  // Probe on undriven_2
  // Probe on inverter_8bit_1_out_invert
  // Probe on adder_8bit_1_sum
  Adder_8Bit adder_8bit_1 (
    .A(inverter_8bit_1_out_invert), .CarryIn(button_1_out), .B(undriven_2), .Sum(adder_8bit_1_sum),
    .Overflow(adder_8bit_1_overflow));  // open: CarryOut
  // Probe on adder_8bit_1_overflow
endmodule

module SignFlag (
  input  [7:0] A,
  output Out_Sign
);


  assign Out_Sign = A[7];
endmodule

module ParityFlag (
  input  [7:0] A,
  output Out_Parity
);

  wire xor_1_out, xor_2_out, xor_3_out, xor_4_out, xor_5_out, xor_6_out, xor_7_out;

  xor xor_1 (xor_1_out, A[0], A[1]);
  xor xor_2 (xor_2_out, A[2], A[3]);
  xor xor_3 (xor_3_out, A[4], A[5]);
  xor xor_4 (xor_4_out, A[6], A[7]);
  xor xor_5 (xor_5_out, xor_1_out, xor_2_out);
  xor xor_6 (xor_6_out, xor_3_out, xor_4_out);
  xor xor_7 (xor_7_out, xor_5_out, xor_6_out);
  not not_1 (Out_Parity, xor_7_out);
endmodule
